// Logisim project cpu-pipelined.circ as structural Verilog: 2 circuits, main circuit main
module main (
  input  [15:0] INSTRUCTION,
  input  CLOCK,
  output [15:0] FETCH_ADDRESS,
  output [15:0] L_s0_Value_7c9fba82,
  output [15:0] L_s1_Value_2cb75696,
  output [15:0] L_s2_Value_be7b1681,
  output [15:0] L_ra_Value_55886cf9,
  output [15:0] L_sp_Value_a0856b3d,
  output [15:0] L_HI_Value_3bde5b98,
  output [15:0] L_LO_Value_b62659ce
);

  wire ALU_Src, and_9_out, and_10_out, Branch, comparator_2_eq, comparator_3_eq, comparator_4_eq,
       comparator_5_eq, comparator_6_eq, comparator_7_eq, comparator_8_eq, comparator_9_eq, equal, Ext,
       JUMPs, KILL, Mem_toReg, Mem_W_R, not_2_out, Op_Add, Op_Addi, Op_And, Op_Andi, Op_Beq, Op_Bne, Op_Jr,
       Op_JumpL, Op_Lh, Op_Lui, Op_Mfhi, Op_Mflo, Op_Mult, Op_Or, Op_Ori, Op_SLL, Op_SLT, Op_Slti, Op_SRL,
       Op_Xor, or_1_out, or_3_out, or_5_out, or_10_out, or_11_out, or_12_out, or_13_out, R_Type, Reg_Dst,
       Reg_Write, U_Instruction;
  wire [1:0] rd_U;
  wire [2:0] ALU_Control, bit_extender_2_out, funct, multiplexer_2_out, multiplexer_3_out, multiplexer_8_out,
       multiplexer_10_out, multiplexer_12_out, multiplexer_15_out, multiplexer_16_out, multiplexer_19_out,
       multiplexer_20_out, rd, rs, rt;
  wire [3:0] opcode;
  wire [5:0] imm_I;
  wire [9:0] imm_U;
  wire [15:0] adder_1_out, adder_2_out, ALU_Result, and_11_out, bit_extender_1_out, bit_extender_3_out,
       bit_extender_4_out, bit_extender_5_out, bit_extender_6_out, bit_extender_7_out, Lui, MEM_p5,
       multiplexer_1_out, multiplexer_4_out, multiplexer_5_out, multiplexer_7_out, multiplexer_9_out,
       multiplexer_11_out, multiplexer_14_out, multiplexer_17_out, multiplexer_18_out, next_PC, Pipeline_q,
       R1, R2, Result2, subtractor_1_out, subtractor_2_out, var_Jr, var_JumpL, Write_Data, Y;

  Register #(.width(16)) L_PC_bd1e00e6 (.D(next_PC), .en(1'b1), .clk(CLOCK), .Q(FETCH_ADDRESS));  // open: clr
  or or_1 (or_1_out, Op_Mult, Op_Lui);
  assign bit_extender_1_out = {{6{1'b0}}, imm_U};  // Bit_Extender bit_extender_1
  Register #(.width(16)) L_LO_ba622f5d (
    .D(multiplexer_1_out), .en(or_1_out), .clk(CLOCK), .Q(L_LO_Value_b62659ce));  // open: clr
  Multiplexer #(.width(16), .enable("false")) multiplexer_1 (
    .in0(ALU_Result), .in1(Lui), .out(multiplexer_1_out), .sel(Op_Lui));
  Register #(.width(16)) L_HI_1d3f3066 (.D(Result2), .en(Op_Mult), .clk(CLOCK), .Q(L_HI_Value_3bde5b98));  // open: clr
  Shifter #(.width(16)) shifter_1 (.in(bit_extender_1_out), .\dist (4'b0110), .out(Lui));
  not not_1 (Mem_toReg, Op_Lh);
  Comparator #(.width(4)) comparator_1 (.a(opcode), .b(4'b0000), .eq(R_Type));  // open: gt, lt
  Comparator #(.width(3)) comparator_2 (.a(funct), .b(3'b000), .eq(comparator_2_eq));  // open: gt, lt
  Comparator #(.width(3)) comparator_3 (.a(funct), .b(3'b001), .eq(comparator_3_eq));  // open: gt, lt
  Comparator #(.width(3)) comparator_4 (.a(funct), .b(3'b010), .eq(comparator_4_eq));  // open: gt, lt
  Comparator #(.width(3)) comparator_5 (.a(funct), .b(3'b011), .eq(comparator_5_eq));  // open: gt, lt
  Comparator #(.width(3)) comparator_6 (.a(funct), .b(3'b100), .eq(comparator_6_eq));  // open: gt, lt
  Comparator #(.width(3)) comparator_7 (.a(funct), .b(3'b101), .eq(comparator_7_eq));  // open: gt, lt
  Comparator #(.width(3)) comparator_8 (.a(funct), .b(3'b110), .eq(comparator_8_eq));  // open: gt, lt
  Comparator #(.width(3)) comparator_9 (.a(funct), .b(3'b111), .eq(comparator_9_eq));  // open: gt, lt
  not not_2 (not_2_out, equal);
  or or_2 (JUMPs, Op_JumpL, Op_Jr);
  or or_3 (or_3_out, Op_Mult, Op_Beq, Op_Bne, Op_Lui, Mem_W_R);
  and and_1 (Op_SLL, comparator_2_eq, R_Type);
  and and_2 (Op_SRL, comparator_3_eq, R_Type);
  and and_3 (Op_Add, comparator_4_eq, R_Type);
  and and_4 (Op_And, comparator_5_eq, R_Type);
  and and_5 (Op_Or, comparator_6_eq, R_Type);
  and and_6 (Op_Xor, comparator_7_eq, R_Type);
  and and_7 (Op_SLT, comparator_8_eq, R_Type);
  and and_8 (Op_Mult, comparator_9_eq, R_Type);
  and and_9 (and_9_out, Op_Beq, equal);
  and and_10 (and_10_out, not_2_out, Op_Bne);
  assign bit_extender_2_out = {{1{1'b0}}, rd_U};  // Bit_Extender bit_extender_2
  not not_3 (Reg_Write, or_3_out);
  or or_4 (Branch, and_9_out, and_10_out);
  Multiplexer #(.width(3), .enable("false")) multiplexer_2 (
    .in0(rd), .in1(bit_extender_2_out), .out(multiplexer_2_out), .sel(U_Instruction));
  Multiplexer #(.width(3), .enable("false")) multiplexer_3 (.in0(rt), .in1(rd), .out(multiplexer_3_out), .sel(Reg_Dst));
  assign bit_extender_3_out = {{10{imm_I[5]}}, imm_I};  // Bit_Extender bit_extender_3
  Multiplexer #(.width(16), .enable("false")) multiplexer_4 (
    .in0(bit_extender_3_out), .in1(bit_extender_4_out), .out(multiplexer_4_out), .sel(Ext));
  assign bit_extender_4_out = {{10{1'b0}}, imm_I};  // Bit_Extender bit_extender_4
  or or_5 (or_5_out, R_Type, Op_Beq, Op_Bne);
  not not_4 (ALU_Src, or_5_out);
  Comparator #(.width(4)) comparator_10 (.a(opcode), .b(4'b0001), .eq(Op_Lui));  // open: gt, lt
  Comparator #(.width(4)) comparator_11 (.a(opcode), .b(4'b0010), .eq(Op_JumpL));  // open: gt, lt
  Comparator #(.width(4)) comparator_12 (.a(opcode), .b(4'b0011), .eq(Op_Jr));  // open: gt, lt
  Comparator #(.width(4)) comparator_13 (.a(opcode), .b(4'b0100), .eq(Op_Beq));  // open: gt, lt
  Comparator #(.width(4)) comparator_14 (.a(opcode), .b(4'b0101), .eq(Op_Bne));  // open: gt, lt
  Comparator #(.width(4)) comparator_15 (.a(opcode), .b(4'b0110), .eq(Op_Addi));  // open: gt, lt
  Comparator #(.width(4)) comparator_16 (.a(opcode), .b(4'b0111), .eq(Op_Slti));  // open: gt, lt
  Subtractor #(.width(16)) subtractor_1 (.a(FETCH_ADDRESS), .b(16'h2), .out(subtractor_1_out));  // open: bin, bout
  assign bit_extender_5_out = {{10{imm_I[5]}}, imm_I};  // Bit_Extender bit_extender_5
  regfile_main main_1 (
    .Read_Register_1_eca808b4(rs), .Read_Register_2_4b336a3e(multiplexer_3_out),
    .Write_Register_1c78e1ef(multiplexer_2_out), .Write_Data_00073c80(Write_Data),
    .Write_Enable_5f560963(Reg_Write), .Clock(CLOCK), .Read_Data_1_c47ea0d8(R1), .Read_Data_2_34b29906(R2),
    .L_s0_Value_3e1de553(L_s0_Value_7c9fba82), .L_s1_Value_f16d02bf(L_s1_Value_2cb75696),
    .L_s2_Value_6a9ed51f(L_s2_Value_be7b1681), .L_ra_Value_b804995d(L_ra_Value_55886cf9),
    .L_sp_Value_269f0ffd(L_sp_Value_a0856b3d));
  Multiplexer #(.width(16), .enable("false")) multiplexer_5 (
    .in0(multiplexer_4_out), .in1(Lui), .out(multiplexer_5_out), .sel(Op_Lui));
  or or_6 (U_Instruction, Op_Lui, Op_JumpL);
  Adder #(.width(16)) adder_1 (.a(FETCH_ADDRESS), .b(16'h2), .out(adder_1_out));  // open: cin, cout
  or or_7 (Ext, Op_Andi, Op_Ori);
  or or_8 (KILL, Branch, JUMPs);
  Multiplexer #(.width(16), .enable("false")) multiplexer_6 (.in0(R2), .in1(multiplexer_5_out), .out(Y), .sel(ALU_Src));
  Adder #(.width(16)) adder_2 (.a(subtractor_1_out), .b(bit_extender_5_out), .out(adder_2_out));  // open: cin, cout
  or or_9 (Reg_Dst, Op_Bne, Mem_W_R, Op_Beq);
  Comparator #(.width(4)) comparator_17 (.a(opcode), .b(4'b1000), .eq(Op_Andi));  // open: gt, lt
  Comparator #(.width(4)) comparator_18 (.a(opcode), .b(4'b1001), .eq(Op_Ori));  // open: gt, lt
  Comparator #(.width(4)) comparator_19 (.a(opcode), .b(4'b1010), .eq(Op_Lh));  // open: gt, lt
  Comparator #(.width(4)) comparator_20 (.a(opcode), .b(4'b1011), .eq(Mem_W_R));  // open: gt, lt
  Comparator #(.width(4)) comparator_21 (.a(opcode), .b(4'b1100), .eq(Op_Mfhi));  // open: gt, lt
  Comparator #(.width(4)) comparator_22 (.a(opcode), .b(4'b1101), .eq(Op_Mflo));  // open: gt, lt
  Multiplexer #(.width(16), .enable("false")) multiplexer_7 (
    .in0(adder_1_out), .in1(adder_2_out), .out(multiplexer_7_out), .sel(Branch));
  alu_main main_2 (
    .Switch(ALU_Control), .X(R1), .Equal(equal), .Result(ALU_Result), .Y(Y), .Result_2_a9898de3(Result2));
  Multiplexer #(.width(3), .enable("false")) multiplexer_8 (
    .in0(3'b000), .in1(3'b000), .out(multiplexer_8_out), .sel(Op_SLL));
  Multiplexer #(.width(16), .enable("false")) multiplexer_9 (
    .in0(multiplexer_7_out), .in1(var_JumpL), .out(multiplexer_9_out), .sel(Op_JumpL));
  Multiplexer #(.width(3), .enable("false")) multiplexer_10 (
    .in0(multiplexer_8_out), .in1(3'b001), .out(multiplexer_10_out), .sel(Op_SRL));
  Multiplexer #(.width(16), .enable("false")) multiplexer_11 (
    .in0(INSTRUCTION), .in1({16{1'b0}}), .out(multiplexer_11_out), .sel(KILL));
  // mem_main MEM: pin names not known; wires that end beside it: ALU_Result, R2, Mem_W_R, CLOCK, MEM_p5
  or or_10 (or_10_out, Op_Add, Op_Addi, Op_Lh, Mem_W_R);
  Register #(.width(16)) Pipeline (.D(multiplexer_11_out), .clk(CLOCK), .Q(Pipeline_q));  // open: en, clr
  Multiplexer #(.width(3), .enable("false")) multiplexer_12 (
    .in0(multiplexer_10_out), .in1(3'b010), .out(multiplexer_12_out), .sel(or_10_out));
  or or_11 (or_11_out, Op_And, Op_Andi);
  Multiplexer #(.width(16), .enable("false")) multiplexer_13 (
    .in0(multiplexer_9_out), .in1(var_Jr), .out(next_PC), .sel(Op_Jr));
  Multiplexer #(.width(16), .enable("false")) multiplexer_14 (
    .in0(MEM_p5), .in1(ALU_Result), .out(multiplexer_14_out), .sel(Mem_toReg));
  Multiplexer #(.width(3), .enable("false")) multiplexer_15 (
    .in0(multiplexer_12_out), .in1(3'b011), .out(multiplexer_15_out), .sel(or_11_out));
  Subtractor #(.width(16)) subtractor_2 (.a(FETCH_ADDRESS), .b(16'h2), .out(subtractor_2_out));  // open: bin, bout
  Multiplexer #(.width(3), .enable("false")) multiplexer_16 (
    .in0(multiplexer_15_out), .in1(3'b100), .out(multiplexer_16_out), .sel(or_12_out));
  or or_12 (or_12_out, Op_Or, Op_Ori);
  assign bit_extender_6_out = {{6{imm_U[9]}}, imm_U};  // Bit_Extender bit_extender_6
  assign bit_extender_7_out = {{10{imm_I[5]}}, imm_I};  // Bit_Extender bit_extender_7
  Multiplexer #(.width(16), .enable("false")) multiplexer_17 (
    .in0(multiplexer_14_out), .in1(L_HI_Value_3bde5b98), .out(multiplexer_17_out), .sel(Op_Mfhi));
  InstructionSplitter instructionsplitter_1 (
    .Instruction(Pipeline_q), .opcode(opcode), .rd(rd), .rs(rs), .rt(rt), .funct(funct), .immediate_I(imm_I),
    .immediate_U(imm_U), .rd_U(rd_U));
  assign and_11_out = subtractor_2_out & 16'hfc00;  // AND_Gate and_11, 16 bits wide
  Multiplexer #(.width(16), .enable("false")) multiplexer_18 (
    .in0(multiplexer_17_out), .in1(L_LO_Value_b62659ce), .out(multiplexer_18_out), .sel(Op_Mflo));
  Multiplexer #(.width(3), .enable("false")) multiplexer_19 (
    .in0(multiplexer_16_out), .in1(3'b101), .out(multiplexer_19_out), .sel(Op_Xor));
  or or_13 (or_13_out, Op_SLT, Op_Slti);
  Adder #(.width(16)) adder_3 (.a(bit_extender_7_out), .b(R1), .out(var_Jr));  // open: cin, cout
  Multiplexer #(.width(3), .enable("false")) multiplexer_20 (
    .in0(multiplexer_19_out), .in1(3'b110), .out(multiplexer_20_out), .sel(or_13_out));
  Multiplexer #(.width(16), .enable("false")) multiplexer_21 (
    .in0(multiplexer_18_out), .in1(FETCH_ADDRESS), .out(Write_Data), .sel(JUMPs));
  Multiplexer #(.width(3), .enable("false")) multiplexer_22 (
    .in0(multiplexer_20_out), .in1(3'b111), .out(ALU_Control), .sel(Op_Mult));
  Adder #(.width(16)) adder_4 (.a(and_11_out), .b(bit_extender_6_out), .out(var_JumpL));  // open: cin, cout

  // Other names for the same wires on the sheet: clk = CLOCK; fetch_addr[15:0] = FETCH_ADDRESS;
  //   HI[15:0] = L_HI_Value_3bde5b98; LO[15:0] = L_LO_Value_b62659ce; Op_Sh = Mem_W_R; ra[15:0] = L_ra_Value_55886cf9;
  //   s0[15:0] = L_s0_Value_7c9fba82; s1[15:0] = L_s1_Value_2cb75696; s2[15:0] = L_s2_Value_be7b1681;
  //   sp[15:0] = L_sp_Value_a0856b3d

  // Notes on the sheet:
  //   Output
  //   These are outputs/inputs from run.circ
  //   Inputs
  //   These are DEBUG/TEST outputs from your circuit.
endmodule

module InstructionSplitter (
  input  [15:0] Instruction,
  output [3:0] opcode,
  output [2:0] rd,
  output [2:0] rs,
  output [2:0] rt,
  output [2:0] funct,
  output [5:0] immediate_I,
  output [9:0] immediate_U,
  output [1:0] rd_U
);


  assign funct = Instruction[2:0];
  assign immediate_I = Instruction[5:0];
  assign immediate_U = Instruction[9:0];
  assign opcode = Instruction[15:12];
  assign rd = Instruction[11:9];
  assign rd_U = Instruction[11:10];
  assign rs = Instruction[8:6];
  assign rt = Instruction[5:3];

  // Notes on the sheet:
  //   Instruction
  //   opcode
  //   rd
  //   rs
  //   rt
  //   funct
  //   immediate-I
  //   immediate-U
endmodule
