// Logisim project regfile.circ as structural Verilog: 1 circuit, main circuit main
module main (
  input  [2:0] Read_Register_1_eca808b4,
  input  [2:0] Read_Register_2_4b336a3e,
  input  [2:0] Write_Register_1c78e1ef,
  input  [15:0] Write_Data_00073c80,
  input  Write_Enable_5f560963,
  input  Clock,
  output [15:0] L_s0_Value_3e1de553,
  output [15:0] L_s1_Value_f16d02bf,
  output [15:0] L_s2_Value_6a9ed51f,
  output [15:0] L_ra_Value_b804995d,
  output [15:0] L_sp_Value_269f0ffd,
  output [15:0] Read_Data_1_c47ea0d8,
  output [15:0] Read_Data_2_34b29906
);

  wire reg0_chosen, reg1_chosen, reg2_chosen, reg3_chosen, reg4_chosen, reg5_chosen, reg6_chosen, reg7_chosen;
  wire [15:0] reg0, reg5, reg6;

  Demultiplexer #(.select(3), .enable("false")) demultiplexer_1 (
    .out0(reg0_chosen), .out1(reg1_chosen), .out2(reg2_chosen), .out3(reg3_chosen), .out4(reg4_chosen),
    .out5(reg5_chosen), .out6(reg6_chosen), .out7(reg7_chosen), .in(Write_Enable_5f560963),
    .sel(Write_Register_1c78e1ef));
  Multiplexer #(.select(3), .width(16), .enable("false")) multiplexer_1 (
    .in0(reg0), .in1(L_ra_Value_b804995d), .in2(L_s0_Value_3e1de553), .in3(L_s1_Value_f16d02bf),
    .in4(L_s2_Value_6a9ed51f), .in5(reg5), .in6(reg6), .in7(L_sp_Value_269f0ffd), .out(Read_Data_1_c47ea0d8),
    .sel(Read_Register_1_eca808b4));
  Multiplexer #(.select(3), .width(16), .enable("false")) multiplexer_2 (
    .in0(reg0), .in1(L_ra_Value_b804995d), .in2(L_s0_Value_3e1de553), .in3(L_s1_Value_f16d02bf),
    .in4(L_s2_Value_6a9ed51f), .in5(reg5), .in6(reg6), .in7(L_sp_Value_269f0ffd), .out(Read_Data_2_34b29906),
    .sel(Read_Register_2_4b336a3e));
  Register #(.width(16)) zero (.D({16{1'b0}}), .en(reg0_chosen), .clk(Clock), .Q(reg0), .clr(1'b1));
  Register #(.width(16)) s2 (
    .D(Write_Data_00073c80), .en(reg4_chosen), .clk(Clock), .Q(L_s2_Value_6a9ed51f));  // open: clr
  Register #(.width(16)) ra (
    .D(Write_Data_00073c80), .en(reg1_chosen), .clk(Clock), .Q(L_ra_Value_b804995d));  // open: clr
  Register #(.width(16)) a0 (.D(Write_Data_00073c80), .en(reg5_chosen), .clk(Clock), .Q(reg5));  // open: clr
  Register #(.width(16)) s0 (
    .D(Write_Data_00073c80), .en(reg2_chosen), .clk(Clock), .Q(L_s0_Value_3e1de553));  // open: clr
  Register #(.width(16)) v0 (.D(Write_Data_00073c80), .en(reg6_chosen), .clk(Clock), .Q(reg6));  // open: clr
  Register #(.width(16)) s1 (
    .D(Write_Data_00073c80), .en(reg3_chosen), .clk(Clock), .Q(L_s1_Value_f16d02bf));  // open: clr
  Register #(.width(16)) sp (
    .D(Write_Data_00073c80), .en(reg7_chosen), .clk(Clock), .Q(L_sp_Value_269f0ffd));  // open: clr

  // Other names for the same wires on the sheet: clk = Clock; read_data1[15:0] = Read_Data_1_c47ea0d8;
  //   read_data2[15:0] = Read_Data_2_34b29906; read_reg1[2:0] = Read_Register_1_eca808b4;
  //   read_reg2[2:0] = Read_Register_2_4b336a3e; reg1[15:0] = L_ra_Value_b804995d; reg2[15:0] = L_s0_Value_3e1de553;
  //   reg3[15:0] = L_s1_Value_f16d02bf; reg4[15:0] = L_s2_Value_6a9ed51f; reg7[15:0] = L_sp_Value_269f0ffd;
  //   write_data[15:0] = Write_Data_00073c80; write_en = Write_Enable_5f560963;
  //   write_reg[2:0] = Write_Register_1c78e1ef

  // Notes on the sheet:
  //   INPUTS to your circuit
  //   DON'T CHANGE THE LOCATIONS OF THE INPUTS AND OUTPUTS!
  //   These are DEBUG/TEST outputs from your circuit.
  //   OUTPUTS from your circuit
endmodule
