// Logisim project cpu.circ as structural Verilog: 2 circuits, main circuit main
module main (
  input  [15:0] INSTRUCTION,
  input  CLOCK,
  output [15:0] FETCH_ADDRESS,
  output [15:0] L_s0_Value_7c9fba82,
  output [15:0] L_s1_Value_2cb75696,
  output [15:0] L_s2_Value_be7b1681,
  output [15:0] L_ra_Value_55886cf9,
  output [15:0] L_sp_Value_a0856b3d,
  output [15:0] L_HI_Value_3bde5b98,
  output [15:0] L_LO_Value_b62659ce
);

  wire ALU_Src, and_3_out, and_4_out, Branch, equal, Ext, JUMPs, KILL, Mem_toReg, Mem_W_R, not_2_out,
       not_3_out, not_4_out, not_5_out, not_6_out, not_7_out, not_8_out, not_9_out, not_10_out, not_11_out,
       not_12_out, not_13_out, not_14_out, not_15_out, not_16_out, not_17_out, not_18_out, not_20_out,
       not_21_out, not_22_out, not_23_out, not_24_out, not_25_out, not_26_out, not_27_out, not_28_out,
       not_30_out, not_31_out, not_32_out, not_33_out, not_34_out, not_35_out, not_36_out, not_37_out,
       not_38_out, not_39_out, not_40_out, not_41_out, not_42_out, not_43_out, not_44_out, not_45_out,
       not_46_out, not_47_out, Op_Add, Op_Addi, Op_And, Op_Andi, Op_Beq, Op_Bne, Op_Jr, Op_JumpL, Op_Lh,
       Op_Lui, Op_Mfhi, Op_Mflo, Op_Mult, Op_Or, Op_Ori, Op_SLL, Op_SLT, Op_Slti, Op_SRL, Op_Xor, or_1_out,
       or_3_out, or_5_out, or_10_out, or_11_out, or_12_out, or_13_out, R_Type, Reg_Dst, Reg_Write,
       U_Instruction;
  wire [1:0] rd_U;
  wire [2:0] ALU_Control, bit_extender_2_out, funct, multiplexer_3_out, multiplexer_4_out, multiplexer_8_out,
       multiplexer_9_out, multiplexer_11_out, multiplexer_13_out, multiplexer_14_out, multiplexer_15_out,
       multiplexer_18_out, rd, rs, rt;
  wire [3:0] opcode;
  wire [5:0] imm_I;
  wire [9:0] imm_U;
  wire [15:0] adder_1_out, adder_2_out, ALU_Result, and_25_out, bit_extender_1_out, bit_extender_3_out,
       bit_extender_4_out, bit_extender_5_out, bit_extender_6_out, bit_extender_7_out, Lui, MEM_p5,
       multiplexer_1_out, multiplexer_2_out, multiplexer_5_out, multiplexer_6_out, multiplexer_10_out,
       multiplexer_12_out, multiplexer_17_out, multiplexer_19_out, multiplexer_21_out, next_PC, Pipeline_q,
       R1, R2, Result2, subtractor_1_out, subtractor_2_out, var_Jr, var_JumpL, Write_Data, Y;

  Register #(.width(16)) L_PC_bd1e00e6 (.D(next_PC), .en(1'b1), .clk(CLOCK), .Q(FETCH_ADDRESS));  // open: clr
  or or_1 (or_1_out, Op_Mult, Op_Lui);
  assign bit_extender_1_out = {{6{1'b0}}, imm_U};  // Bit_Extender bit_extender_1
  Register #(.width(16)) L_LO_ba622f5d (
    .D(multiplexer_1_out), .en(or_1_out), .clk(CLOCK), .Q(L_LO_Value_b62659ce));  // open: clr
  Multiplexer #(.width(16), .enable("false")) multiplexer_1 (
    .in0(ALU_Result), .in1(Lui), .out(multiplexer_1_out), .sel(Op_Lui));
  Register #(.width(16)) L_HI_1d3f3066 (.D(Result2), .en(Op_Mult), .clk(CLOCK), .Q(L_HI_Value_3bde5b98));  // open: clr
  Shifter #(.width(16)) shifter_1 (.in(bit_extender_1_out), .\dist (4'b0110), .out(Lui));
  not not_1 (Mem_toReg, Op_Lh);
  not not_2 (not_2_out, equal);
  not not_3 (not_3_out, opcode[1]);
  not not_4 (not_4_out, opcode[0]);
  not not_5 (not_5_out, opcode[3]);
  not not_6 (not_6_out, opcode[2]);
  and and_1 (R_Type, not_5_out, not_6_out, not_3_out, not_4_out);
  not not_7 (not_7_out, funct[0]);
  not not_8 (not_8_out, funct[1]);
  not not_9 (not_9_out, funct[2]);
  and and_2 (Op_SLL, R_Type, not_9_out, not_8_out, not_7_out);
  and and_3 (and_3_out, Op_Beq, equal);
  and and_4 (and_4_out, not_2_out, Op_Bne);
  or or_2 (JUMPs, Op_JumpL, Op_Jr);
  Multiplexer #(.width(16), .enable("false")) multiplexer_2 (
    .in0(INSTRUCTION), .in1({16{1'b0}}), .out(multiplexer_2_out), .sel(KILL));
  not not_10 (not_10_out, opcode[1]);
  not not_11 (not_11_out, opcode[3]);
  not not_12 (not_12_out, opcode[2]);
  and and_5 (Op_Lui, not_11_out, not_12_out, not_10_out, opcode[0]);
  not not_13 (not_13_out, funct[1]);
  not not_14 (not_14_out, funct[2]);
  and and_6 (Op_SRL, R_Type, not_14_out, not_13_out, funct[0]);
  or or_3 (or_3_out, Op_Mult, Op_Beq, Op_Bne, Op_Lui, Mem_W_R);
  or or_4 (Branch, and_3_out, and_4_out);
  Register #(.width(16)) Pipeline (.D(multiplexer_2_out), .clk(CLOCK), .Q(Pipeline_q));  // open: en, clr
  not not_15 (not_15_out, opcode[2]);
  not not_16 (not_16_out, opcode[3]);
  and and_7 (Op_JumpL, not_16_out, not_15_out, opcode[1], not_20_out);
  not not_17 (not_17_out, funct[2]);
  not not_18 (not_18_out, funct[0]);
  and and_8 (Op_Add, R_Type, not_17_out, funct[1], not_18_out);
  assign bit_extender_2_out = {{1{1'b0}}, rd_U};  // Bit_Extender bit_extender_2
  not not_19 (Reg_Write, or_3_out);
  not not_20 (not_20_out, opcode[0]);
  not not_21 (not_21_out, opcode[3]);
  not not_22 (not_22_out, opcode[2]);
  not not_23 (not_23_out, funct[2]);
  and and_9 (Op_And, R_Type, not_23_out, funct[1], funct[0]);
  Multiplexer #(.width(3), .enable("false")) multiplexer_3 (
    .in0(rd), .in1(bit_extender_2_out), .out(multiplexer_3_out), .sel(U_Instruction));
  not not_24 (not_24_out, opcode[3]);
  and and_10 (Op_Jr, not_21_out, not_22_out, opcode[1], opcode[0]);
  and and_11 (Op_Or, R_Type, funct[2], not_27_out, not_28_out);
  Multiplexer #(.width(3), .enable("false")) multiplexer_4 (.in0(rt), .in1(rd), .out(multiplexer_4_out), .sel(Reg_Dst));
  assign bit_extender_3_out = {{10{imm_I[5]}}, imm_I};  // Bit_Extender bit_extender_3
  Multiplexer #(.width(16), .enable("false")) multiplexer_5 (
    .in0(bit_extender_3_out), .in1(bit_extender_4_out), .out(multiplexer_5_out), .sel(Ext));
  assign bit_extender_4_out = {{10{1'b0}}, imm_I};  // Bit_Extender bit_extender_4
  or or_5 (or_5_out, R_Type, Op_Beq, Op_Bne);
  InstructionSplitter instructionsplitter_1 (
    .Instruction(Pipeline_q), .opcode(opcode), .rd(rd), .rs(rs), .rt(rt), .funct(funct), .immediate_I(imm_I),
    .immediate_U(imm_U), .rd_U(rd_U));
  not not_25 (not_25_out, opcode[1]);
  not not_26 (not_26_out, opcode[0]);
  and and_12 (Op_Beq, not_24_out, opcode[2], not_25_out, not_26_out);
  not not_27 (not_27_out, funct[1]);
  not not_28 (not_28_out, funct[0]);
  not not_29 (ALU_Src, or_5_out);
  or or_6 (U_Instruction, Op_Lui, Op_JumpL);
  not not_30 (not_30_out, opcode[1]);
  not not_31 (not_31_out, opcode[3]);
  and and_13 (Op_Bne, not_31_out, opcode[2], not_30_out, opcode[0]);
  not not_32 (not_32_out, funct[1]);
  and and_14 (Op_Xor, R_Type, funct[2], not_32_out, funct[0]);
  Subtractor #(.width(16)) subtractor_1 (.a(FETCH_ADDRESS), .b(16'h2), .out(subtractor_1_out));  // open: bin, bout
  assign bit_extender_5_out = {{10{imm_I[5]}}, imm_I};  // Bit_Extender bit_extender_5
  regfile_main main_1 (
    .Read_Register_1_eca808b4(rs), .Read_Register_2_4b336a3e(multiplexer_4_out),
    .Write_Register_1c78e1ef(multiplexer_3_out), .Write_Data_00073c80(Write_Data),
    .Write_Enable_5f560963(Reg_Write), .Clock(CLOCK), .Read_Data_1_c47ea0d8(R1), .Read_Data_2_34b29906(R2),
    .L_s0_Value_3e1de553(L_s0_Value_7c9fba82), .L_s1_Value_f16d02bf(L_s1_Value_2cb75696),
    .L_s2_Value_6a9ed51f(L_s2_Value_be7b1681), .L_ra_Value_b804995d(L_ra_Value_55886cf9),
    .L_sp_Value_269f0ffd(L_sp_Value_a0856b3d));
  Multiplexer #(.width(16), .enable("false")) multiplexer_6 (
    .in0(multiplexer_5_out), .in1(Lui), .out(multiplexer_6_out), .sel(Op_Lui));
  or or_7 (KILL, Branch, JUMPs);
  not not_33 (not_33_out, opcode[3]);
  not not_34 (not_34_out, opcode[0]);
  and and_15 (Op_Addi, not_33_out, opcode[2], opcode[1], not_34_out);
  not not_35 (not_35_out, funct[0]);
  and and_16 (Op_SLT, R_Type, funct[2], funct[1], not_35_out);
  Adder #(.width(16)) adder_1 (.a(FETCH_ADDRESS), .b(16'h2), .out(adder_1_out));  // open: cin, cout
  or or_8 (Ext, Op_Andi, Op_Ori);
  not not_36 (not_36_out, opcode[3]);
  and and_17 (Op_Slti, not_36_out, opcode[2], opcode[1], opcode[0]);
  and and_18 (Op_Mult, R_Type, funct[2], funct[1], funct[0]);
  Multiplexer #(.width(16), .enable("false")) multiplexer_7 (.in0(R2), .in1(multiplexer_6_out), .out(Y), .sel(ALU_Src));
  Adder #(.width(16)) adder_2 (.a(subtractor_1_out), .b(bit_extender_5_out), .out(adder_2_out));  // open: cin, cout
  or or_9 (Reg_Dst, Op_Bne, Mem_W_R, Op_Beq);
  Multiplexer #(.width(3), .enable("false")) multiplexer_8 (
    .in0(3'b000), .in1(3'b000), .out(multiplexer_8_out), .sel(Op_SLL));
  not not_37 (not_37_out, opcode[1]);
  not not_38 (not_38_out, opcode[2]);
  not not_39 (not_39_out, opcode[0]);
  and and_19 (Op_Andi, opcode[3], not_38_out, not_37_out, not_39_out);
  Multiplexer #(.width(3), .enable("false")) multiplexer_9 (
    .in0(multiplexer_8_out), .in1(3'b001), .out(multiplexer_9_out), .sel(Op_SRL));
  not not_40 (not_40_out, opcode[1]);
  not not_41 (not_41_out, opcode[2]);
  and and_20 (Op_Ori, opcode[3], not_41_out, not_40_out, opcode[0]);
  Multiplexer #(.width(16), .enable("false")) multiplexer_10 (
    .in0(adder_1_out), .in1(adder_2_out), .out(multiplexer_10_out), .sel(Branch));
  alu_main main_2 (
    .Switch(ALU_Control), .X(R1), .Equal(equal), .Result(ALU_Result), .Y(Y), .Result_2_a9898de3(Result2));
  or or_10 (or_10_out, Op_Add, Op_Addi, Op_Lh, Mem_W_R);
  not not_42 (not_42_out, opcode[2]);
  not not_43 (not_43_out, opcode[0]);
  and and_21 (Op_Lh, opcode[3], not_42_out, opcode[1], not_43_out);
  Multiplexer #(.width(3), .enable("false")) multiplexer_11 (
    .in0(multiplexer_9_out), .in1(3'b010), .out(multiplexer_11_out), .sel(or_10_out));
  or or_11 (or_11_out, Op_And, Op_Andi);
  not not_44 (not_44_out, opcode[2]);
  and and_22 (Mem_W_R, opcode[3], not_44_out, opcode[1], opcode[0]);
  Multiplexer #(.width(16), .enable("false")) multiplexer_12 (
    .in0(multiplexer_10_out), .in1(var_JumpL), .out(multiplexer_12_out), .sel(Op_JumpL));
  Multiplexer #(.width(3), .enable("false")) multiplexer_13 (
    .in0(multiplexer_11_out), .in1(3'b011), .out(multiplexer_13_out), .sel(or_11_out));
  and and_23 (Op_Mfhi, opcode[3], opcode[2], not_45_out, not_46_out);
  // mem_main MEM: pin names not known; wires that end beside it: ALU_Result, R2, Mem_W_R, CLOCK, MEM_p5
  Multiplexer #(.width(3), .enable("false")) multiplexer_14 (
    .in0(multiplexer_13_out), .in1(3'b100), .out(multiplexer_14_out), .sel(or_12_out));
  or or_12 (or_12_out, Op_Or, Op_Ori);
  not not_45 (not_45_out, opcode[1]);
  not not_46 (not_46_out, opcode[0]);
  Multiplexer #(.width(3), .enable("false")) multiplexer_15 (
    .in0(multiplexer_14_out), .in1(3'b101), .out(multiplexer_15_out), .sel(Op_Xor));
  not not_47 (not_47_out, opcode[1]);
  and and_24 (Op_Mflo, opcode[3], opcode[2], not_47_out, opcode[0]);
  Multiplexer #(.width(16), .enable("false")) multiplexer_16 (
    .in0(multiplexer_12_out), .in1(var_Jr), .out(next_PC), .sel(Op_Jr));
  Multiplexer #(.width(16), .enable("false")) multiplexer_17 (
    .in0(MEM_p5), .in1(ALU_Result), .out(multiplexer_17_out), .sel(Mem_toReg));
  or or_13 (or_13_out, Op_SLT, Op_Slti);
  Subtractor #(.width(16)) subtractor_2 (.a(FETCH_ADDRESS), .b(16'h2), .out(subtractor_2_out));  // open: bin, bout
  Multiplexer #(.width(3), .enable("false")) multiplexer_18 (
    .in0(multiplexer_15_out), .in1(3'b110), .out(multiplexer_18_out), .sel(or_13_out));
  assign bit_extender_6_out = {{6{imm_U[9]}}, imm_U};  // Bit_Extender bit_extender_6
  assign bit_extender_7_out = {{10{imm_I[5]}}, imm_I};  // Bit_Extender bit_extender_7
  Multiplexer #(.width(16), .enable("false")) multiplexer_19 (
    .in0(multiplexer_17_out), .in1(L_HI_Value_3bde5b98), .out(multiplexer_19_out), .sel(Op_Mfhi));
  Multiplexer #(.width(3), .enable("false")) multiplexer_20 (
    .in0(multiplexer_18_out), .in1(3'b111), .out(ALU_Control), .sel(Op_Mult));
  assign and_25_out = subtractor_2_out & 16'hfc00;  // AND_Gate and_25, 16 bits wide
  Multiplexer #(.width(16), .enable("false")) multiplexer_21 (
    .in0(multiplexer_19_out), .in1(L_LO_Value_b62659ce), .out(multiplexer_21_out), .sel(Op_Mflo));
  Adder #(.width(16)) adder_3 (.a(bit_extender_7_out), .b(R1), .out(var_Jr));  // open: cin, cout
  Multiplexer #(.width(16), .enable("false")) multiplexer_22 (
    .in0(multiplexer_21_out), .in1(FETCH_ADDRESS), .out(Write_Data), .sel(JUMPs));
  Adder #(.width(16)) adder_4 (.a(and_25_out), .b(bit_extender_6_out), .out(var_JumpL));  // open: cin, cout

  // Other names for the same wires on the sheet: clk = CLOCK; fetch_addr[15:0] = FETCH_ADDRESS;
  //   HI[15:0] = L_HI_Value_3bde5b98; LO[15:0] = L_LO_Value_b62659ce; Op_Sh = Mem_W_R; ra[15:0] = L_ra_Value_55886cf9;
  //   s0[15:0] = L_s0_Value_7c9fba82; s1[15:0] = L_s1_Value_2cb75696; s2[15:0] = L_s2_Value_be7b1681;
  //   sp[15:0] = L_sp_Value_a0856b3d

  // Notes on the sheet:
  //   Output
  //   These are outputs/inputs from run.circ
  //   Inputs
  //   These are DEBUG/TEST outputs from your circuit.
endmodule

module InstructionSplitter (
  input  [15:0] Instruction,
  output [3:0] opcode,
  output [2:0] rd,
  output [2:0] rs,
  output [2:0] rt,
  output [2:0] funct,
  output [5:0] immediate_I,
  output [9:0] immediate_U,
  output [1:0] rd_U
);


  assign funct = Instruction[2:0];
  assign immediate_I = Instruction[5:0];
  assign immediate_U = Instruction[9:0];
  assign opcode = Instruction[15:12];
  assign rd = Instruction[11:9];
  assign rd_U = Instruction[11:10];
  assign rs = Instruction[8:6];
  assign rt = Instruction[5:3];

  // Notes on the sheet:
  //   Instruction
  //   opcode
  //   rd
  //   rs
  //   rt
  //   funct
  //   immediate-I
  //   immediate-U
endmodule
