// Logisim project alu.circ as structural Verilog: 1 circuit, main circuit main
module main (
  input  [15:0] X,
  input  [15:0] Y,
  input  [2:0] Switch,
  output Equal,
  output [15:0] Result,
  output [15:0] Result_2_a9898de3
);

  wire comparator_1_lt;
  wire [15:0] adder_1_out, and_1_out, bit_extender_1_out, multiplier_1_out, or_1_out, shifter_1_out,
       shifter_2_out, xor_1_out;

  Shifter #(.width(16)) shifter_1 (.in(X), .\dist (Y[3:0]), .out(shifter_1_out));
  Shifter #(.width(16), .shift("lr")) shifter_2 (.in(X), .\dist (Y[3:0]), .out(shifter_2_out));
  Adder #(.width(16)) adder_1 (.a(X), .b(Y), .out(adder_1_out));  // open: cin, cout
  assign and_1_out = X & Y;  // AND_Gate and_1, 16 bits wide
  assign or_1_out = X | Y;  // OR_Gate or_1, 16 bits wide
  assign xor_1_out = X ^ Y;  // XOR_Gate xor_1, 16 bits wide
  Comparator #(.width(16)) comparator_1 (.a(X), .b(Y), .eq(Equal), .lt(comparator_1_lt));  // open: gt
  Multiplier #(.width(16)) multiplier_1 (.a(X), .b(Y), .out(multiplier_1_out), .cout(Result_2_a9898de3));  // open: cin
  assign bit_extender_1_out = {{15{1'b0}}, comparator_1_lt};  // Bit_Extender bit_extender_1
  Multiplexer #(.select(3), .width(16), .enable("false")) multiplexer_1 (
    .in0(shifter_1_out), .in1(shifter_2_out), .in2(adder_1_out), .in3(and_1_out), .in4(or_1_out),
    .in5(xor_1_out), .in6(bit_extender_1_out), .in7(multiplier_1_out), .out(Result), .sel(Switch));

  // Other names for the same wires on the sheet: result_2[15:0] = Result_2_a9898de3; S[2:0] = Switch

  // Notes on the sheet:
  //   INPUTS to your circuit
  //   DON'T CHANGE THE LOCATIONS OF THE INPUTS AND OUTPUTS!
  //   OUTPUTS from your circuit
endmodule
