// Logisim project cpu.circ as structural Verilog: 1 circuit, main circuit main
module main (
  input  [15:0] INSTRUCTION,
  input  CLOCK,
  output [15:0] FETCH_ADDRESS,
  output [15:0] L_s0_Value_7c9fba82,
  output [15:0] L_s1_Value_2cb75696,
  output [15:0] L_s2_Value_be7b1681,
  output [15:0] L_ra_Value_55886cf9,
  output [15:0] L_sp_Value_a0856b3d,
  output [15:0] L_HI_Value_3bde5b98,
  output [15:0] L_LO_Value_b62659ce,
  output [2:0] out_11,
  output [2:0] out_12,
  output [2:0] out_13,
  output [15:0] out_14,
  output [15:0] out_15,
  output [2:0] out_16,
  output [15:0] out_17,
  output [15:0] out_18,
  output [15:0] out_19,
  output [1:0] out_20
);

  wire and_1_out, and_2_out, and_3_out, and_5_out, Comp_Eq, comparator_1_eq, comparator_2_eq,
       comparator_3_eq, comparator_4_eq, comparator_6_eq, comparator_7_eq, comparator_8_eq, F_0, F_Mult,
       multiplexer_6_out, not_1_out, not_2_out, not_3_out, not_4_out, not_5_out, or_1_out, or_2_out;
  wire [1:0] X_Sel, Y_Sel;
  wire [2:0] RD_U;
  wire [3:0] multiplexer_1_out, OPCode;
  wire [15:0] adder_2_out, I_0_Ex, I_Sig_Ex, main_1_read_data_1_c47ea0d8, main_2_result_2_a9898de3,
       multiplexer_2_out, multiplexer_8_out, multiplexer_9_out, PC_2, PC_JUMP, r2, RAM_DATA, shifter_1_out,
       shifter_2_out, shifter_5_out, shifter_6_out, shifter_8_out, WRITE_DATA;

  Register #(.width(16)) L_PC_bd1e00e6 (.D(multiplexer_2_out), .clk(CLOCK), .Q(FETCH_ADDRESS));  // open: en, clr
  Comparator #(.width(4)) comparator_1 (.a(OPCode), .b(4'b0100), .eq(comparator_1_eq));  // open: gt, lt
  Comparator #(.width(4)) comparator_2 (.a(OPCode), .b(4'b0101), .eq(comparator_2_eq));  // open: gt, lt
  not not_1 (not_1_out, Comp_Eq);
  not not_2 (not_2_out, comparator_2_eq);
  not not_3 (not_3_out, comparator_1_eq);
  and and_1 (and_1_out, not_2_out, not_3_out);
  Comparator #(.width(4)) comparator_3 (.a(OPCode), .b(4'b1011), .eq(comparator_3_eq));  // open: gt, lt
  Comparator #(.width(3)) comparator_4 (.a(INSTRUCTION[2:0]), .b(3'b111), .eq(comparator_4_eq));  // open: gt, lt
  Adder #(.width(16)) adder_1 (.a(FETCH_ADDRESS), .b(16'h2), .out(PC_2));  // open: cin, cout
  Adder #(.width(16)) adder_2 (.a(I_Sig_Ex), .b(FETCH_ADDRESS), .out(adder_2_out));  // open: cin, cout
  and and_2 (and_2_out, comparator_1_eq, Comp_Eq);
  and and_3 (and_3_out, comparator_2_eq, not_1_out);
  // mem_main MEM: pin names not known; wires that end beside it: out_14, r2, comparator_3_eq, CLOCK, RAM_DATA
  assign RD_U = {{1{1'b0}}, INSTRUCTION[11:10]};  // Bit_Extender bit_extender_1
  and and_4 (F_Mult, comparator_4_eq, F_0);
  Multiplexer #(.width(4), .enable("false")) multiplexer_1 (
    .in0(4'b0000), .in1(OPCode), .out(multiplexer_1_out), .sel(or_1_out));
  or or_1 (or_1_out, and_2_out, and_3_out, and_1_out);
  Multiplexer #(.select(4), .width(16), .enable("false")) multiplexer_2 (
    .in0(PC_2), .in1(PC_2), .in2(PC_JUMP), .in3(out_14), .in4(adder_2_out), .in5(adder_2_out), .in6(PC_2),
    .in7(PC_2), .in8(PC_2), .in9(PC_2), .in10(PC_2), .in11(PC_2), .in12(PC_2), .in13(PC_2), .in14(PC_2),
    .in15(PC_2), .out(multiplexer_2_out), .sel(multiplexer_1_out));
  Shifter #(.width(16), .shift("lr")) shifter_1 (.in(INSTRUCTION), .\dist (4'b1100), .out(shifter_1_out));
  Bit_Extender #(.in_width(16), .out_width(4), .\type ("zero")) bit_extender_2 (.in(shifter_1_out), .out(OPCode));
  Shifter #(.width(16)) shifter_2 (.in(INSTRUCTION), .\dist (4'b1010), .out(shifter_2_out));
  not not_4 (not_4_out, F_0);
  Comparator #(.width(16)) comparator_5 (.a(shifter_1_out), .b({16{1'b0}}), .eq(F_0));  // open: gt, lt
  Shifter #(.width(16), .shift("ar")) shifter_3 (.in(shifter_2_out), .\dist (4'b1010), .out(I_Sig_Ex));
  Shifter #(.width(16), .shift("lr")) shifter_4 (.in(shifter_2_out), .\dist (4'b1010), .out(I_0_Ex));
  Multiplexer #(.select(4), .width(16), .enable("false")) multiplexer_3 (
    .in0(out_14), .in1(out_14), .in2(PC_2), .in3(PC_2), .in4(out_14), .in5(out_14), .in6(out_14),
    .in7(out_14), .in8(out_14), .in9(out_14), .in10(RAM_DATA), .in11(out_14), .in12(L_HI_Value_3bde5b98),
    .in13(L_LO_Value_b62659ce), .in14(out_14), .in15(out_14), .out(WRITE_DATA), .sel(OPCode));
  Multiplexer #(.width(3), .enable("false")) multiplexer_4 (
    .in0(INSTRUCTION[5:3]), .in1(INSTRUCTION[11:9]), .out(out_12), .sel(not_4_out));
  Comparator #(.width(4)) comparator_6 (.a(OPCode), .b(4'b0010), .eq(comparator_6_eq));  // open: gt, lt
  Multiplexer #(.width(3), .enable("false")) multiplexer_5 (
    .in0(INSTRUCTION[11:9]), .in1(RD_U), .out(out_11), .sel(comparator_6_eq));
  and and_5 (and_5_out, not_5_out, multiplexer_6_out);
  not not_5 (not_5_out, F_Mult);
  Multiplexer #(.select(4), .enable("false")) multiplexer_6 (
    .in0(1'b1), .in1(1'b0), .in2(1'b1), .in3(1'b1), .in4(1'b0), .in5(1'b0), .in6(1'b1), .in7(1'b1),
    .in8(1'b1), .in9(1'b1), .in10(1'b1), .in11(1'b0), .in12(1'b1), .in13(1'b1), .in14(1'b1), .in15(1'b1),
    .out(multiplexer_6_out), .sel(OPCode));
  regfile_main main_1 (
    .Read_Register_1_eca808b4(INSTRUCTION[8:6]), .Read_Register_2_4b336a3e(out_12),
    .Write_Register_1c78e1ef(out_11), .Write_Data_00073c80(WRITE_DATA), .Write_Enable_5f560963(and_5_out),
    .Clock(CLOCK), .Read_Data_1_c47ea0d8(main_1_read_data_1_c47ea0d8), .Read_Data_2_34b29906(r2),
    .L_s0_Value_3e1de553(L_s0_Value_7c9fba82), .L_s1_Value_f16d02bf(L_s1_Value_2cb75696),
    .L_s2_Value_6a9ed51f(L_s2_Value_be7b1681), .L_ra_Value_b804995d(L_ra_Value_55886cf9),
    .L_sp_Value_269f0ffd(L_sp_Value_a0856b3d));
  Comparator #(.width(4)) comparator_7 (.a(OPCode), .b(4'b0001), .eq(comparator_7_eq));  // open: gt, lt
  Multiplexer #(.width(2), .enable("false")) multiplexer_7 (
    .in0(2'b00), .in1(2'b01), .out(X_Sel), .sel(comparator_7_eq));
  Multiplexer #(.select(2), .width(16), .enable("false")) multiplexer_8 (
    .in0(main_1_read_data_1_c47ea0d8), .in1(INSTRUCTION), .out(multiplexer_8_out), .sel(X_Sel));  // open: in2, in3
  alu_main main_2 (
    .Switch(out_16), .X(multiplexer_8_out), .Equal(Comp_Eq), .Result(out_14), .Y(multiplexer_9_out),
    .Result_2_a9898de3(main_2_result_2_a9898de3));
  Multiplexer #(.select(2), .width(16), .enable("false")) multiplexer_9 (
    .in0(r2), .in1(16'h6), .in2(I_Sig_Ex), .in3(I_0_Ex), .out(multiplexer_9_out), .sel(Y_Sel));
  Multiplexer #(.select(4), .width(3), .enable("false")) multiplexer_10 (
    .in0(INSTRUCTION[2:0]), .in3(3'b010), .in6(3'b010), .in7(3'b110), .in8(3'b011), .in9(3'b100),
    .in10(3'b010), .in11(3'b010), .out(out_16), .sel(OPCode));  // open: in1, in2, in4, in5, in12, in13, in14, in15
  Multiplexer #(.select(4), .width(2), .enable("false")) multiplexer_11 (
    .in0(2'b00), .in1(2'b01), .in2(2'b00), .in3(2'b10), .in4(2'b00), .in5(2'b00), .in6(2'b10), .in7(2'b10),
    .in8(2'b11), .in9(2'b11), .in10(2'b10), .in11(2'b10), .in12(2'b00), .in13(2'b00), .in14(2'b00),
    .in15(2'b00), .out(Y_Sel), .sel(OPCode));
  or or_2 (or_2_out, F_Mult, comparator_8_eq);
  Comparator #(.width(4)) comparator_8 (.a(OPCode), .b(4'b0001), .eq(comparator_8_eq));  // open: gt, lt
  Register #(.width(16)) L_HI_1d3f3066 (
    .D(main_2_result_2_a9898de3), .en(F_Mult), .clk(CLOCK), .Q(L_HI_Value_3bde5b98));  // open: clr
  Register #(.width(16)) L_LO_ba622f5d (.D(out_14), .en(or_2_out), .clk(CLOCK), .Q(L_LO_Value_b62659ce));  // open: clr
  Shifter #(.width(16)) shifter_5 (.in(INSTRUCTION), .\dist (4'b0110), .out(shifter_5_out));
  Shifter #(.width(16), .shift("lr")) shifter_6 (.in(FETCH_ADDRESS), .\dist (4'b1010), .out(shifter_6_out));
  Shifter #(.width(16), .shift("lr")) shifter_7 (.in(shifter_5_out), .\dist (4'b0110), .out(out_19));
  Shifter #(.width(16)) shifter_8 (.in(shifter_6_out), .\dist (4'b1010), .out(shifter_8_out));
  Adder #(.width(16)) adder_3 (.a(out_19), .b(shifter_8_out), .out(PC_JUMP));  // open: cin, cout

  assign out_13 = INSTRUCTION[8:6];
  assign out_18 = out_14;
  assign out_20 = INSTRUCTION[11:10];

  // Other names for the same wires on the sheet: ALU_R[15:0] = out_14; clk = CLOCK; fetch_addr[15:0] = FETCH_ADDRESS;
  //   PC[15:0] = FETCH_ADDRESS; HI_OUT[15:0] = L_HI_Value_3bde5b98; Funct[2:0] = INSTRUCTION[2:0];
  //   rt[2:0] = INSTRUCTION[5:3]; rs[2:0] = INSTRUCTION[8:6]; rd[2:0] = INSTRUCTION[11:9];
  //   LO_OUT[15:0] = L_LO_Value_b62659ce

  // Notes on the sheet:
  //   Output
  //   These are outputs/inputs from run.circ
  //   Inputs
  //   These are DEBUG/TEST outputs from your circuit.
  //   Immediate Sign Extended
  //   Immediate Zero Extended
endmodule
