// Logisim project regfile.circ as structural Verilog: 2 circuits, main circuit main
module main (
  input  [2:0] Read_Register_1_eca808b4,
  input  [2:0] Read_Register_2_4b336a3e,
  input  [2:0] Write_Register_1c78e1ef,
  input  [15:0] Write_Data_00073c80,
  input  Write_Enable_5f560963,
  input  Clock,
  output [15:0] L_s0_Value_3e1de553,
  output [15:0] L_s1_Value_f16d02bf,
  output [15:0] L_s2_Value_6a9ed51f,
  output [15:0] L_ra_Value_b804995d,
  output [15:0] L_sp_Value_269f0ffd,
  output [15:0] Read_Data_1_c47ea0d8,
  output [15:0] Read_Data_2_34b29906
);

  wire demultiplexer_1_out1, demultiplexer_1_out2, demultiplexer_1_out3, demultiplexer_1_out4,
       demultiplexer_1_out5, demultiplexer_1_out6, demultiplexer_1_out7;
  wire [15:0] Reg_0_q, Reg_a0_q, Reg_v0_q;

  Demultiplexer #(.select(3), .enable("false")) demultiplexer_1 (
    .out1(demultiplexer_1_out1), .out2(demultiplexer_1_out2), .out3(demultiplexer_1_out3),
    .out4(demultiplexer_1_out4), .out5(demultiplexer_1_out5), .out6(demultiplexer_1_out6),
    .out7(demultiplexer_1_out7), .in(Write_Enable_5f560963), .sel(Write_Register_1c78e1ef));  // open: out0
  Register #(.width(16)) Reg_0 (.D(Write_Data_00073c80), .clk(Clock), .Q(Reg_0_q), .clr(Clock));  // open: en
  Register #(.width(16)) Reg_ra (
    .D(Write_Data_00073c80), .en(demultiplexer_1_out1), .clk(Clock), .Q(L_ra_Value_b804995d));  // open: clr
  Register #(.width(16)) Reg_s0 (
    .D(Write_Data_00073c80), .en(demultiplexer_1_out2), .clk(Clock), .Q(L_s0_Value_3e1de553));  // open: clr
  Register #(.width(16)) Reg_s1 (
    .D(Write_Data_00073c80), .en(demultiplexer_1_out3), .clk(Clock), .Q(L_s1_Value_f16d02bf));  // open: clr
  Register #(.width(16)) Reg_s2 (
    .D(Write_Data_00073c80), .en(demultiplexer_1_out4), .clk(Clock), .Q(L_s2_Value_6a9ed51f));  // open: clr
  Register #(.width(16)) Reg_a0 (
    .D(Write_Data_00073c80), .en(demultiplexer_1_out5), .clk(Clock), .Q(Reg_a0_q));  // open: clr
  Register #(.width(16)) Reg_v0 (
    .D(Write_Data_00073c80), .en(demultiplexer_1_out6), .clk(Clock), .Q(Reg_v0_q));  // open: clr
  Register #(.width(16)) Reg_sp (
    .D(Write_Data_00073c80), .en(demultiplexer_1_out7), .clk(Clock), .Q(L_sp_Value_269f0ffd));  // open: clr
  Multiplexer #(.select(3), .width(16), .enable("false")) multiplexer_1 (
    .in0(Reg_0_q), .in1(L_ra_Value_b804995d), .in2(L_s0_Value_3e1de553), .in3(L_s1_Value_f16d02bf),
    .in4(L_s2_Value_6a9ed51f), .in5(Reg_a0_q), .in6(Reg_v0_q), .in7(L_sp_Value_269f0ffd),
    .out(Read_Data_1_c47ea0d8), .sel(Read_Register_1_eca808b4));
  Multiplexer #(.select(3), .width(16), .enable("false")) multiplexer_2 (
    .in0(Reg_0_q), .in1(L_ra_Value_b804995d), .in2(L_s0_Value_3e1de553), .in3(L_s1_Value_f16d02bf),
    .in4(L_s2_Value_6a9ed51f), .in5(Reg_a0_q), .in6(Reg_v0_q), .in7(L_sp_Value_269f0ffd),
    .out(Read_Data_2_34b29906), .sel(Read_Register_2_4b336a3e));

  // Other names for the same wires on the sheet: clk = Clock; read_data1[15:0] = Read_Data_1_c47ea0d8;
  //   read_data2[15:0] = Read_Data_2_34b29906; read_reg1[2:0] = Read_Register_1_eca808b4;
  //   read_reg2[2:0] = Read_Register_2_4b336a3e; write_data[15:0] = Write_Data_00073c80;
  //   write_en = Write_Enable_5f560963; write_reg[2:0] = Write_Register_1c78e1ef

  // Notes on the sheet:
  //   INPUTS to your circuit
  //   DON'T CHANGE THE LOCATIONS OF THE INPUTS AND OUTPUTS!
  //   These are DEBUG/TEST outputs from your circuit.
  //   OUTPUTS from your circuit
endmodule

module Regs (
  input  [15:0] Write_data_inf,
  input  [15:0] Out_Read_1,
  input  [2:0] Sel_Read_1,
  input  [2:0] Sel_Write,
  input  [15:0] Out_Read_2,
  input  [2:0] Sel_Read_2,
  input  Write_Enable,
  input  [15:0] s0_out,
  input  Clock,
  input  [15:0] s1_out,
  input  [15:0] s2_out,
  input  [15:0] ra_out,
  input  [15:0] sp_out
);

  wire [15:0] demultiplexer_1_out1, demultiplexer_1_out2, demultiplexer_1_out3, demultiplexer_1_out4,
       demultiplexer_1_out5, demultiplexer_1_out6, demultiplexer_1_out7, Reg_0_q, Reg_a0_q, Reg_v0_q;

  Demultiplexer #(.select(3), .width(16), .enable("false")) demultiplexer_1 (
    .out1(demultiplexer_1_out1), .out2(demultiplexer_1_out2), .out3(demultiplexer_1_out3),
    .out4(demultiplexer_1_out4), .out5(demultiplexer_1_out5), .out6(demultiplexer_1_out6),
    .out7(demultiplexer_1_out7), .in(Write_data_inf), .sel(Sel_Write));  // open: out0
  Register #(.width(16)) Reg_0 (.en(Write_Enable), .clk(Clock), .Q(Reg_0_q), .clr(Clock));  // open: D
  Register #(.width(16)) Reg_ra (.D(demultiplexer_1_out1), .en(Write_Enable), .clk(Clock), .Q(ra_out));  // open: clr
  Register #(.width(16)) Reg_s0 (.D(demultiplexer_1_out2), .clk(Clock), .Q(s0_out));  // open: en, clr
  Register #(.width(16)) Reg_s1 (.D(demultiplexer_1_out3), .en(Write_Enable), .clk(Clock), .Q(s1_out));  // open: clr
  Register #(.width(16)) Reg_s2 (.D(demultiplexer_1_out4), .en(Write_Enable), .clk(Clock), .Q(s2_out));  // open: clr
  Register #(.width(16)) Reg_a0 (.D(demultiplexer_1_out5), .en(Write_Enable), .clk(Clock), .Q(Reg_a0_q));  // open: clr
  Register #(.width(16)) Reg_v0 (.D(demultiplexer_1_out6), .en(Write_Enable), .clk(Clock), .Q(Reg_v0_q));  // open: clr
  Register #(.width(16)) Reg_sp (.D(demultiplexer_1_out7), .en(Write_Enable), .clk(Clock), .Q(sp_out));  // open: clr
  Multiplexer #(.select(3), .width(16), .enable("false")) multiplexer_1 (
    .in0(Reg_0_q), .in1(ra_out), .in2(s0_out), .in3(s1_out), .in4(s2_out), .in5(Reg_a0_q), .in6(Reg_v0_q),
    .in7(sp_out), .out(Out_Read_1), .sel(Sel_Read_1));
  Multiplexer #(.select(3), .width(16), .enable("false")) multiplexer_2 (
    .in0(Reg_0_q), .in1(ra_out), .in2(s0_out), .in3(s1_out), .in4(s2_out), .in5(Reg_a0_q), .in6(Reg_v0_q),
    .in7(sp_out), .out(Out_Read_2), .sel(Sel_Read_2));
endmodule
